# Fritzing sketch schema (saved by Fritzing 0.9.3b)

parts:
  WeMos_D1_Mini1 = WeMos D1 Mini
  Součástka1 = Adafruit SHT31-D Sensirion Temperature/Humidity Sensor [part_number="Adafruit #2857"]
  S2 = Reed switch [package=THT]

nets:
  N1: WeMos_D1_Mini1.3V3, S2.pin_1
  5V: WeMos_D1_Mini1.5V, Součástka1.VIN
  N2: WeMos_D1_Mini1.D0, WeMos_D1_Mini1.RST
  N3: WeMos_D1_Mini1.D1, Součástka1.SCL
  N4: WeMos_D1_Mini1.D2, Součástka1.SDA
  N5: WeMos_D1_Mini1.D5, S2.pin_2
  N6: WeMos_D1_Mini1.G, Součástka1.GND

notes:
  Magnetick locker

custom parts:
  Adafruit SHT31-D Sensirion Temperature/Humidity Sensor: Sensirion Temperature/Humidity sensors are some of the finest & highest-accuracy devices you can get. And, finally we have some that have a true I2C interface for easy reading. The SHT31-D sensor has an excellent ±2% relative humidity and ±0.3°C accuracy for most uses. Unlike earlier SHT sensors, this sensor has a true I2C interface, and (bonus!) even with two address options. It also is 3V or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
